# Fritzing sketch ledplatte_ (saved by Fritzing 0.9.3b)

parts:
  Bauteil5 = Arduino Uno (Rev3) - ICSP
  NEOPIXEL24 = Neopixel Strip -- Black (30/m)
  NEOPIXEL25 = Neopixel Strip -- Black (30/m)
  NEOPIXEL26 = Neopixel Strip -- Black (30/m)
  NEOPIXEL27 = Neopixel Strip -- Black (30/m)
  NEOPIXEL28 = Neopixel Strip -- Black (30/m)
  NEOPIXEL29 = Neopixel Strip -- Black (30/m)
  NEOPIXEL30 = Neopixel Strip -- Black (30/m)
  NEOPIXEL31 = Neopixel Strip -- Black (30/m)
  NEOPIXEL32 = Neopixel Strip -- Black (30/m)
  NEOPIXEL33 = Neopixel Strip -- Black (30/m)
  JACK4 = 2.1mm Barrel Jack with Terminal Block
  NEOPIXEL34 = Neopixel Strip -- Black (30/m)

nets:
  N1: Bauteil5.GND, NEOPIXEL29.GND#1, JACK4.NEG
  N2: Bauteil5.D5_PWM, NEOPIXEL29.Din
  N3: NEOPIXEL24.GND#1, NEOPIXEL29.GND#6
  N4: NEOPIXEL24.Din, NEOPIXEL29.Dout
  N5: NEOPIXEL24.+5V#3, NEOPIXEL29.+5V#4
  N6: NEOPIXEL24.+5V#4, NEOPIXEL33.+5V#3
  N7: NEOPIXEL24.Dout, NEOPIXEL33.Din
  N8: NEOPIXEL24.GND#6, NEOPIXEL33.GND#1
  N9: NEOPIXEL25.GND#1, NEOPIXEL31.GND#6
  N10: NEOPIXEL25.Din, NEOPIXEL31.Dout
  N11: NEOPIXEL25.+5V#3, NEOPIXEL31.+5V#4
  N12: NEOPIXEL25.+5V#4, NEOPIXEL30.+5V#3
  N13: NEOPIXEL25.Dout, NEOPIXEL30.Din
  N14: NEOPIXEL25.GND#6, NEOPIXEL30.GND#1
  N15: NEOPIXEL26.GND#1, NEOPIXEL30.GND#6
  N16: NEOPIXEL26.Din, NEOPIXEL30.Dout
  N17: NEOPIXEL26.+5V#3, NEOPIXEL30.+5V#4
  N18: NEOPIXEL26.+5V#4, NEOPIXEL32.+5V
  N19: NEOPIXEL26.Dout, NEOPIXEL32.Din
  N20: NEOPIXEL26.GND#6, NEOPIXEL32.GND
  N21: NEOPIXEL27.GND#1, NEOPIXEL33.GND#6
  N22: NEOPIXEL27.Din, NEOPIXEL33.Dout
  N23: NEOPIXEL27.+5V#3, NEOPIXEL33.+5V#4
  N24: NEOPIXEL27.+5V#4, NEOPIXEL28.+5V#3
  N25: NEOPIXEL27.Dout, NEOPIXEL28.Din
  N26: NEOPIXEL27.GND#6, NEOPIXEL28.GND#1
  N27: NEOPIXEL28.+5V#4, NEOPIXEL34.+5V#3
  N28: NEOPIXEL28.Dout, NEOPIXEL34.Din
  N29: NEOPIXEL28.GND#6, NEOPIXEL34.GND#1
  N30: NEOPIXEL29.+5V#3, JACK4.POS
  N31: NEOPIXEL31.GND#1, NEOPIXEL34.GND#6
  N32: NEOPIXEL31.Din, NEOPIXEL34.Dout
  N33: NEOPIXEL31.+5V#3, NEOPIXEL34.+5V#4

custom parts:
  Neopixel Strip -- Black (30/m): These NeoPixel strips have 30 digitally-addressable pixel LEDs per meter and are very affordable and are only 12.5 mm wide, 10 mm if you remove the strip from the casing.
